# Fritzing sketch Spark Core demo (saved by Fritzing 0.9.1b)
breadboards: 1

parts:
  Part1 = Spark Core (v1.0)
  LED1 = smd LED [color="Red (633nm)" package="0603 [SMD]"]
  S1 = Toggle Switch [package=THT]
  U1 = POT [part_number=10k package=alps_pot]
  R1 = Resistor [tolerance=±5% resistance=470 package=THT]

nets:
  N1: Part1.A0, U1.S
  N2: Part1.GND, LED1.cathode, S1.L2, U1.E
  N3: Part1.D0, R1.Pin_0
  N4: Part1.D1, S1.COM
  N5: Part1.3V3*, S1.L1, U1.A
  N6: LED1.anode, R1.Pin_1
